# Fritzing sketch wiringPiPotentiometerExampleSPI (saved by Fritzing 0.7.12b)
breadboards: 1

parts:
  RaspberryPi1 = Raspberry Pi Model B
  IC1 = MCP3008 8-channel 10-bit ADC [part_number=MCP3008]
  R1 = Basic Potentiometer [package=THT]
  Pi1 = Adafruit Pi Cobbler

nets:
  3V3: RaspberryPi1.3V3, IC1.no_name_yet#8, R1.leg2, Pi1.3V3
  N1: IC1.no_name_yet#1, IC1.no_name_yet#6, R1.leg1, Pi1.GND
  N2: IC1.no_name_yet#2, Pi1.CE0
  N3: IC1.no_name_yet#3, Pi1.MOSI
  N4: IC1.no_name_yet#4, Pi1.MISO
  N5: IC1.no_name_yet#5, Pi1.SCLK
  N6: IC1.no_name_yet#9, R1.wiper

custom parts:
  Raspberry Pi Model B: Raspberry Pi (Model B)
  Adafruit Pi Cobbler: Adafruit Pi Cobbler GPIO Breakout for Raspberry Pi
