# Fritzing sketch wiringPiPotentiometerExampleSPI (saved by Fritzing 0.7.12b)
breadboards: 1

parts:
  Pi1 = Adafruit Pi Cobbler
  RaspberryPi1 = Raspberry Pi Model B
  IC1 = MCP3008 8-channel 10-bit ADC [part_number=MCP3008]
  R1 = Basic Potentiometer [package=THT]

nets:
  3V3: Pi1.3V3, RaspberryPi1.3V3, IC1.no_name_yet#8, R1.leg2
  N1: Pi1.GND, IC1.no_name_yet#1, IC1.no_name_yet#6, R1.leg1
  N2: Pi1.MOSI, IC1.no_name_yet#3
  N3: Pi1.MISO, IC1.no_name_yet#4
  N4: Pi1.SCLK, IC1.no_name_yet#5
  N5: Pi1.CE0, IC1.no_name_yet#2
  N6: Pi1.PIN25, RaspberryPi1.CS1
  N7: IC1.no_name_yet#9, R1.wiper

custom parts:
  Adafruit Pi Cobbler: Adafruit Pi Cobbler GPIO Breakout for Raspberry Pi
  Raspberry Pi Model B: Raspberry Pi (Model B)
